// Logisim project TrabalhoULA.circ as structural Verilog: 4 circuits, main circuit Shift Registrer
module Shift_Registrer (
  input  in_1,
  input  in_2,
  output out_3,
  output out_4,
  output out_5,
  output out_6,
  output out_7,
  output out_8,
  output out_9,
  output out_10,
  output out_11
);

  D_Flip_Flop d_ff_1 (.clk(in_1), .D(in_2), .Q(out_4));  // open: Qn, preset, en, reset
  D_Flip_Flop d_ff_2 (.clk(in_1), .D(out_4), .Q(out_5));  // open: Qn, preset, en, reset
  D_Flip_Flop d_ff_3 (.clk(in_1), .D(out_5), .Q(out_6));  // open: Qn, preset, en, reset
  D_Flip_Flop d_ff_4 (.clk(in_1), .D(out_6), .Q(out_7));  // open: Qn, preset, en, reset
  D_Flip_Flop d_ff_5 (.clk(in_1), .D(out_7), .Q(out_8));  // open: Qn, preset, en, reset
  D_Flip_Flop d_ff_6 (.clk(in_1), .D(out_8), .Q(out_9));  // open: Qn, preset, en, reset
  D_Flip_Flop d_ff_7 (.clk(in_1), .D(out_9), .Q(out_10));  // open: Qn, preset, en, reset
  D_Flip_Flop d_ff_8 (.clk(in_1), .D(out_10), .Q(out_3));  // open: Qn, preset, en, reset

  assign out_11 = out_3;

  // Notes on the sheet:
  //   Nomes: Leonardo Preczevski Ramos, Matheus Machado Berwaldt, Davi Oliveira Paris Nunes
endmodule

module Mux (
  input  S0,
  input  S1,
  input  in_3,
  input  in_4,
  input  in_5,
  input  in_6,
  output out_7
);

  wire and_1_out, and_2_out, and_3_out, and_4_out, not_1_out, not_2_out;

  not not_1 (not_1_out, S0);
  not not_2 (not_2_out, S1);
  and and_1 (and_1_out, in_3, not_1_out, not_2_out);
  and and_2 (and_2_out, in_4, not_1_out, S1);
  and and_3 (and_3_out, in_5, S0, not_2_out);
  and and_4 (and_4_out, in_6, S0, S1);
  or or_1 (out_7, and_1_out, and_2_out, and_3_out, and_4_out);

  // Notes on the sheet:
  //   Nomes: Leonardo Preczevski Ramos, Matheus Machado Berwaldt, Davi Oliveira Paris Nunes
endmodule

module App (
  input  B_inverte,
  input  [1:0] in_2
);

  wire and_1_out, clock_1_out, d_ff_1_q, mux_1_out_7, or_1_out, shift_registrer_1_out_3,
       shift_registrer_2_out_3, somador_1_out_4, somador_1_out_5, xor_1_out, xor_2_out;
  wire [3:0] shift_registrer_1_out_7, shift_registrer_1_out_11, shift_registrer_2_out_7,
       shift_registrer_2_out_11;

  Clock clock_1 (.out(clock_1_out));
  Shift_Registrer shift_registrer_1 (
    .in_1(clock_1_out), .in_2(mux_1_out_7), .out_4(shift_registrer_1_out_7[3]),
    .out_5(shift_registrer_1_out_7[2]), .out_6(shift_registrer_1_out_7[1]),
    .out_7(shift_registrer_1_out_7[0]), .out_8(shift_registrer_1_out_11[3]),
    .out_9(shift_registrer_1_out_11[2]), .out_10(shift_registrer_1_out_11[1]),
    .out_11(shift_registrer_1_out_11[0]), .out_3(shift_registrer_1_out_3));
  Shift_Registrer shift_registrer_2 (
    .in_1(clock_1_out), .in_2(1'b0), .out_4(shift_registrer_2_out_7[3]), .out_5(shift_registrer_2_out_7[2]),
    .out_6(shift_registrer_2_out_7[1]), .out_7(shift_registrer_2_out_7[0]),
    .out_8(shift_registrer_2_out_11[3]), .out_9(shift_registrer_2_out_11[2]),
    .out_10(shift_registrer_2_out_11[1]), .out_11(shift_registrer_2_out_11[0]),
    .out_3(shift_registrer_2_out_3));
  Hex_Digit_Display hex_digit_display_1 (.value(shift_registrer_1_out_7));  // open: dp
  and and_1 (and_1_out, shift_registrer_1_out_3, shift_registrer_2_out_3);
  or or_1 (or_1_out, shift_registrer_1_out_3, shift_registrer_2_out_3);
  xor xor_1 (xor_1_out, shift_registrer_1_out_3, shift_registrer_2_out_3);
  xor xor_2 (xor_2_out, shift_registrer_2_out_3, B_inverte);
  Hex_Digit_Display hex_digit_display_2 (.value(shift_registrer_1_out_11));  // open: dp
  Hex_Digit_Display hex_digit_display_3 (.value(shift_registrer_2_out_7));  // open: dp
  Somador somador_1 (
    .in_1(shift_registrer_1_out_3), .in_2(xor_2_out), .in_3(d_ff_1_q), .out_4(somador_1_out_4),
    .out_5(somador_1_out_5));
  Hex_Digit_Display hex_digit_display_4 (.value(shift_registrer_2_out_11));  // open: dp
  D_Flip_Flop d_ff_1 (.clk(clock_1_out), .D(somador_1_out_5), .Q(d_ff_1_q));  // open: Qn, preset, en, reset
  Mux mux_1 (
    .in_3(and_1_out), .in_4(or_1_out), .in_5(xor_1_out), .in_6(somador_1_out_4), .S0(in_2[1]), .S1(in_2[0]),
    .out_7(mux_1_out_7));

  // Notes on the sheet:
  //   Nomes: Leonardo Preczevski Ramos, Matheus Machado Berwaldt, Davi Oliveira Paris Nunes
endmodule

module Somador (
  input  in_1,
  input  in_2,
  input  in_3,
  output out_4,
  output out_5
);

  wire and_1_out, and_2_out, xor_1_out;

  xor xor_1 (xor_1_out, in_1, in_2);
  and and_1 (and_1_out, in_3, xor_1_out);
  and and_2 (and_2_out, in_1, in_2);
  xor xor_2 (out_4, xor_1_out, in_3);
  or or_1 (out_5, and_1_out, and_2_out);

  // Notes on the sheet:
  //   Nomes: Leonardo Preczevski Ramos, Matheus Machado Berwaldt, Davi Oliveira Paris Nunes
endmodule
